# Fritzing sketch CircuitDemo (saved by Fritzing 0.9.3b)
breadboards: 1

parts:
  DHT1 = Humidity and Temperature Sensor DHT11
  U1 = NodeMCU V1.0
  S1 = SWITCH-MOMENTARY-2 [package=tactile-pth-12mm]
  LED1 = RGB LED - (4 legs) [package="5 mm [THT]"]
  R1 = Resistor [tolerance=±5% resistance=220 package="2010 [SMD]"]
  R2 = Resistor [tolerance=±5% resistance=220 package="2010 [SMD]"]
  R3 = Resistor [tolerance=±5% resistance=220 package="2010 [SMD]"]
  R4 = Resistor [tolerance=±5% resistance=220 package="2512 [SMD]"]
  Part1 = LCD1602-I2C
  R5 = Resistor [tolerance=±5% resistance=220 package="2010 [SMD]"]

nets:
  VCC: DHT1.Vcc, U1.3V3, S1.2, LED1.green_cathode, R3.Pin_0
  N1: DHT1.Data-signal, U1.D4, R3.Pin_1
  GND: DHT1.GND_2, U1.GND, R4.Pin_1, Part1.GND
  N2: U1.D1, Part1.SCL
  N3: U1.D2, Part1.SDA
  N4: U1.D6, R1.Pin_1
  N5: U1.D7, R5.Pin_1
  N6: U1.D8, R2.Pin_0
  VIN: U1.Vin, Part1.VCC
  N7: S1.1, R4.Pin_0
  N8: LED1.red_cathode, R5.Pin_0
  N9: LED1.common_anode, R2.Pin_1
  N10: LED1.blue_cathode, R1.Pin_0

custom parts:
  Humidity and Temperature Sensor DHT11: Digital relative humidity & temperature sensor DHT11
  NodeMCU V1.0: ESP8266 based NodeMCU
  LCD1602-I2C: A standard character display, usually with 2x16 characters. Comes in many colors with LCM1602 IIC attached.
